# Fritzing sketch accordion-lamp (saved by Fritzing 1.0.2b)

parts:
  Part1 = Arduino Nano (Rev3.0)
  SERVO1 = Tower Pro SG90 servo [part_number=101246]
  R1 = Resistor [tolerance=±5% power=0.25 resistance=220 package=THT]
  R2 = Resistor [tolerance=±5% power=0.25 resistance=220 package=THT]
  R3 = Resistor [tolerance=±5% power=0.25 resistance=220 package=THT]
  LED2 = RGB LED (com. cathode, rbg) [color="Red (633nm)" current=0.030A package="5 mm [THT]"]

nets:
  GND: Part1.GND, SERVO1.GND, LED2.common_cathode
  N1: Part1.D3, R1.Pin_0
  N2: Part1.D5, R3.Pin_0
  N3: Part1.D6, R2.Pin_0
  N4: Part1.D9, SERVO1.Signal
  5V: Part1.5V, SERVO1.+5V
  N5: R1.Pin_1, LED2.red_anode
  N6: R2.Pin_1, LED2.blue_anode
  N7: R3.Pin_1, LED2.green_anode

custom parts:
  Tower Pro SG90 servo: Original file by John De Cristofaro http://www.adafruit.com/products/1449 Adafruit Feedback Servo (Small) Edited by: e-radionica.com 28/9/2015
