# Fritzing sketch balancing-robot (saved by Fritzing 1.0.2b)
# 18650 Li-ion Battery: CC-BY Dr Kristofer Chan, King's College London/Remote-research.org
breadboards: 1

parts:
  Part1 = Arduino Nano (Rev3.0)
  M1 = RioRand LM2596
  BAT1 = 18650 Li-ion Battery [package=battery-18650]
  BAT2 = 18650 Li-ion Battery [package=battery-18650]
  Mod1 = 2S-BMS
  M2 = gear-motor
  M3 = gear-motor
  Part3 = InvenSense MPU6050
  R1 = Resistor [tolerance=±5% resistance=10k package="1206 [SMD]"]  # not connected
  Part4 = Adafruit DRV8833 DC/Stepper Motor Driver [part_number="Adafruit #3297"]
  M4 = RioRand LM2596
  S1 = Pushbutton [package="[THT]"]
  R2 = Resistor [tolerance=±5% resistance=10k package="0603 [SMD]"]

nets:
  GND: Part1.GND, M1.Pin_4, Part3.GND, Part4.GND, M4.Pin_4, R2.Pin_0
  N1: Part1.D2, S1.Pin_3, S1.Pin_4, R2.Pin_1
  N2: Part1.D3, Part4.NFAULT
  N3: Part1.D5, Part4.AIN1
  N4: Part1.D6, Part4.AIN2
  N5: Part1.D7, Part4.!SLEEP
  N6: Part1.D9, Part4.BIN2
  N7: Part1.D11/MOSI, Part4.BIN1
  5V: Part1.5V, M1.Pin_3, Part3.VCC, S1.Pin_1, S1.Pin_2
  N8: Part1.A5, Part3.SCL
  N9: Part1.A4, Part3.SDA
  N10: M1.Pin_1, Mod1.pin3#3, M4.Pin_1
  N11: M1.Pin_2, Mod1.pin3#2, M4.Pin_2
  N12: BAT1.-, Mod1.pin2
  N13: BAT1.+, BAT2.-, Mod1.pin3#4
  N14: BAT2.+, Mod1.pin1
  N15: M2.pin_1, Part4.AOUT2
  N16: M2.pin_2, Part4.AOUT1
  N17: M3.pin_1, Part4.BOUT1
  N18: M3.pin_2, Part4.BOUT2
  N19: Part4.VMOTOR, M4.Pin_3

custom parts:
  18650 Li-ion Battery: 18650 li-ion Battery Standard 18650 battery with interactive connectors Creative Common Attribution 4.0 International (CC-BY 4.0) license. Any use of this part requires attribution of Dr Kristofer Chan, Department of Geography, King's College London. Contact kristofer.chan [at] kcl.ac.uk OR kris [at] remote-research.org for further information.
  2S-BMS: 2S-BMS LIPO battery charger / protection unit. Note pcb does not match the board as it will likely connect with wires, so pcb is 5 pads suitable for .1in header pins.
  Adafruit DRV8833 DC/Stepper Motor Driver: Spin two DC motors or step one bi-polar or uni-polar stepper with up to 1.2A per channel using the DRV8833. This motor driver chip is a nice alternative to the TB6612 driver. Like that chip, you get 2 full H-bridges, but this chip is better for low voltage uses (can run from 2.7V up to 10.8V motor power) and has built in current limiting capability. We set it up for 1A current limiting so you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
