# Fritzing sketch dustbin-dispenser (saved by Fritzing 0.9.10b)
breadboards: 1

parts:
  Part1 = Arduino Nano (Rev3.0)
  HC-SR04_Sensor_1 = HC-SR04 Ultrasonic Distance Sensor
  HC-SR04_Sensor_2 = HC-SR04 Ultrasonic Distance Sensor
  Servo = Tower Pro SG90 servo [part_number=101246]
  Pump = DC Motor [voltage_(max)=6V voltage_(min)=3V]
  Relay = KY-019 5V Relay Module [package="Breakout board"]

nets:
  N1: Part1.D2, HC-SR04_Sensor_1.TRIG
  N2: Part1.D4, HC-SR04_Sensor_1.ECHO
  N3: Part1.D5, Relay.S
  N4: Part1.D8, HC-SR04_Sensor_2.ECHO
  N5: Part1.D9, HC-SR04_Sensor_2.TRIG
  N6: Part1.D11/MOSI, Servo.Signal
  5V: Part1.VIN, Relay.Common
  GND: Part1.GND, HC-SR04_Sensor_1.GND, HC-SR04_Sensor_2.GND, Servo.GND, Pump.pin_2, Relay.-
  VCC: Part1.5V, HC-SR04_Sensor_1.VCC, HC-SR04_Sensor_2.VCC, Servo.+5V, Relay.+
  N7: Pump.pin_1, Relay.NO

custom parts:
  Tower Pro SG90 servo: Original file by John De Cristofaro http://www.adafruit.com/products/1449 Adafruit Feedback Servo (Small) Edited by: e-radionica.com 28/9/2015
  KY-019 5V Relay Module: KY-019 5V Relay module, used to control AC circuits. (Special thanks to vanepp for fixing the PCB holes and other errors)

// code stored in the sketch: dustbin-dispenser-4.ino
#include <Servo.h>

const float SOUND_SPEED = 0.0343; // centimeter per microsecond at 20 degrees celsius
const int LOOP_DELAY = 100; // millisecond

const int SERVO_PIN = 11; // Must be a PWM Pin
const int SERVO_TRIG_PIN = 9;
const int SERVO_ECHO_PIN = 8;

const int DISPENSER_PIN = 5;
const int DISPENSER_TRIG_PIN = 2;
const int DISPENSER_ECHO_PIN = 4;

// {{{{{ SETTINGS

/* Unit: degree */
unsigned int servo_close_angle = 100; // Servo position where the dust-bin cap is closed.
unsigned int servo_open_angle = 0; // Servo position where the dust-bin cap is opened.

/* Unit: centimeter */
unsigned int servo_max_distance = 20;     // Maximum distance where the servo activates
unsigned int dispenser_max_distance = 4; // Maximum distance where the dispenser activates

/* Unit: millisecond (multiples of LOOP_DELAY) */
unsigned int servo_return_delay = 30;     // Delay before returning the dust-bin cap to closed position
unsigned int dispenser_spit_delay = 1;    // Delay before the dispenser spits a liquid
unsigned int dispenser_spit_duration = 1; // Duration where dispenser spits a liquid continuously after delay

// END }}}}}

bool dispenser_running = false;
unsigned int dispenser_timeout = 0;
unsigned int servo_timeout = 0;

unsigned long duration, time;
float servo_distance, dispenser_distance;

Servo servo;

float echo(int trig_pin, int echo_pin) {
	digitalWrite(trig_pin, LOW); delayMicroseconds(2);
	digitalWrite(trig_pin, HIGH); delayMicroseconds(10);
	digitalWrite(trig_pin, LOW);

	duration = pulseIn(echo_pin, HIGH, 10000);
	return duration ? (duration * SOUND_SPEED) / 2 : 0;
}

void setup() {
	pinMode(DISPENSER_PIN, OUTPUT);
	pinMode(DISPENSER_TRIG_PIN, OUTPUT);
	pinMode(DISPENSER_ECHO_PIN, INPUT);

	pinMode(SERVO_TRIG_PIN, OUTPUT);
	pinMode(SERVO_ECHO_PIN, INPUT);

	digitalWrite(DISPENSER_PIN, HIGH);
	
	servo.attach(SERVO_PIN);
	servo.write(servo_close_angle);

	servo_return_delay *= LOOP_DELAY;
	dispenser_spit_delay *= LOOP_DELAY;
	dispenser_spit_duration *= LOOP_DELAY;
}

void loop() {
	servo_distance = echo(SERVO_TRIG_PIN, SERVO_ECHO_PIN);
	dispenser_distance = echo(DISPENSER_TRIG_PIN, DISPENSER_ECHO_PIN);

	if (servo_distance && servo_distance <= servo_max_distance) {
		if (servo_timeout == 0) servo.write(servo_open_angle);
		servo_timeout = servo_return_delay;
	} else if (servo_timeout && (servo_timeout -= LOOP_DELAY) == 0) servo.write(servo_close_angle);

	if (dispenser_distance && dispenser_distance <= dispenser_max_distance) {
		if (! dispenser_running) {
			dispenser_running = true;
			dispenser_timeout = dispenser_spit_delay + dispenser_spit_duration;
		} else dispenser_timeout -= dispenser_timeout ? LOOP_DELAY : 0;
		digitalWrite(DISPENSER_PIN, (dispenser_timeout && dispenser_timeout <= dispenser_spit_duration) ? LOW : HIGH);
	} else {
		dispenser_running = false;
		dispenser_timeout = 0;
		digitalWrite(DISPENSER_PIN, HIGH);
	}
	delay(LOOP_DELAY);
}
