# Fritzing sketch water-level-meter (saved by Fritzing 1.0.0d)
breadboards: 1

parts:
  HC-SR04_Sensor = HC-SR04 Ultrasonic Distance Sensor
  Buzzer = Piezo Speaker
  R2 = Resistor [tolerance=±5% resistance=1k package="2010 [SMD]"]
  Button = Pushbutton [package="[THT]"]
  Part1 = Arduino Nano (Rev3.0)
  R3 = Rotary Potentiometer (Large) [maximum_resistance=10kΩ knob_status=50% power=0.5W package=THT]
  Part2 = LCD1602-I2C

nets:
  VCC: HC-SR04_Sensor.VCC, Button.Pin_1, Button.Pin_2, Part1.5V, R3.leg2, Part2.VCC
  N1: HC-SR04_Sensor.TRIG, Part1.D5
  N2: HC-SR04_Sensor.ECHO, Part1.D4
  GND: HC-SR04_Sensor.GND, Buzzer.pin1, R2.Pin_0, Part1.GND, R3.leg1, Part2.GND
  N3: Buzzer.pin2, Part1.D6
  N4: R2.Pin_1, Button.Pin_3, Button.Pin_4, Part1.D2
  N5: Part1.A5, Part2.SCL
  N6: Part1.A4, Part2.SDA
  N7: Part1.A0, R3.wiper

custom parts:
  LCD1602-I2C: A standard character display, usually with 2x16 characters. Comes in many colors with LCM1602 IIC attached.
