# Fritzing sketch button-debouncer (saved by Fritzing 1.0.2b)

parts:
  Mod1 = Amica NodeMCU DEVKIT 1.0
  S1 = Pushbutton [package="[THT]"]
  R1 = Resistor [tolerance=±5% resistance=220 package="2512 [SMD]"]

nets:
  N1: Mod1.pin1, S1.Pin_1, S1.Pin_2
  N2: Mod1.pin2, R1.Pin_0
  N3: Mod1.pin_14, S1.Pin_3, S1.Pin_4, R1.Pin_1
