# Fritzing sketch power-monitor (saved by Fritzing 1.0.1rc)
breadboards: 1

parts:
  Mod1 = Amica NodeMCU DEVKIT 1.0
  Part3 = I2C level shifter bidirectional
  OLED_I2C1 = OLED 128x64 I2C Monochrome Display
  HLK-PM1 = HLK-PM01
  ZMPT101B = zmpt101b
  ACS712 = ACS712 Current Sensor 5A 20A 30A
  Part4 = ADS1115
  Input_AC_Voltage = Camdenboss CTB0158-2 [part_number=CTB0158-2 package=THT]
  Fuse_(10_A) = FUSE [package=fuse_5mm]
  Fuse_(300_mA) = FUSE [package=fuse_5mm]
  Output_AC_Voltage_(Load) = Camdenboss CTB0158-2 [part_number=CTB0158-2 package=THT]

nets:
  N1: Mod1.pin1, Part3.LV, OLED_I2C1.VDD
  GND: Mod1.pin2, Mod1.pin_29, Part3.GND, OLED_I2C1.GND, HLK-PM1.-Vo, ZMPT101B.GND#2, ACS712.GND, Part4.GND, Part4.A3
  N2: Mod1.pin_13, Part3.LV2, OLED_I2C1.SDA
  N3: Mod1.pin_14, Part3.LV1, OLED_I2C1.SCK
  VCC: Mod1.pin_30, Part3.HV, HLK-PM1.+Vo, ZMPT101B.VCC, ACS712.VCC, Part4.VDD, Part4.A2
  N4: Part3.HV1, Part4.SCL
  N5: Part3.HV2, Part4.SDA
  N6: HLK-PM1.AC#0, Fuse_(300_mA).2
  N7: HLK-PM1.AC#1, Input_AC_Voltage.pin1, Fuse_(10_A).1
  N8: ZMPT101B.OUT, Part4.A1
  N9: ZMPT101B.N, Fuse_(10_A).2, Output_AC_Voltage_(Load).pin2
  N10: ZMPT101B.L, ACS712.1, Input_AC_Voltage.pin2, Fuse_(300_mA).1
  N11: ACS712.2, ACS712.OUT, Part4.A0, Output_AC_Voltage_(Load).pin1

custom parts:
  zmpt101b: Single phase ac active output voltate transformer module.
  ACS712 Current Sensor 5A 20A 30A: Remix by Michael Kubina http://www.kubina.info Original by: https://forum.fritzing.org/t/current-sensor-5a-acs712/7694 https://forum.fritzing.org/u/ArtHome ArtHome12@gmail.com
  ADS1115: ADC ADS1115
